# Fritzing sketch PulseSensorBeatColor (saved by Fritzing 0.7.10b)
breadboards: 1

parts:
  Arduino1 = Arduino Fio
  LED1 = RGB LED (com. anode, rbg) [package="5 mm [THT]"]
  LED2 = RGB LED (com. anode, rbg) [package="5 mm [THT]"]
  R1 = Resistor [tolerance=±5% resistance=220 package=THT]
  R2 = Resistor [tolerance=±5% resistance=220 package=THT]
  R3 = Resistor [tolerance=±5% resistance=220 package=THT]
  R4 = Resistor [tolerance=±5% resistance=220 package=THT]
  R5 = Resistor [tolerance=±5% resistance=220 package=THT]
  R6 = Resistor [tolerance=±5% resistance=220 package=THT]
  J1 = Infrared Proximity Sensor

nets:
  N1: Arduino1.A0, J1.Vout
  3V3: Arduino1.3V3, Arduino1.AREF, LED1.common_anode, LED2.common_anode, J1.Vcc
  GND: Arduino1.GND, J1.GND
  N2: Arduino1.D3, R6.Pin_1
  N3: Arduino1.D4, R5.Pin_1
  N4: Arduino1.D5, R4.Pin_1
  N5: Arduino1.D6, R3.Pin_1
  N6: Arduino1.D7, R2.Pin_1
  N7: Arduino1.D8, R1.Pin_1
  N8: LED1.red_cathode, R4.Pin_0
  N9: LED1.blue_cathode, R5.Pin_0
  N10: LED1.green_cathode, R6.Pin_0
  N11: LED2.red_cathode, R1.Pin_0
  N12: LED2.blue_cathode, R2.Pin_0
  N13: LED2.green_cathode, R3.Pin_0
